# Fritzing sketch projeto (saved by Fritzing 0.9.4)
breadboards: 1

parts:
  Componente1 = Arduino Uno (Rev3) - ICSP
  RHT1 = Humidity and Temperature Sensor RHT03

nets:
  N1: Componente1.D5_PWM, RHT1.Data-signal
  5V: Componente1.5V, RHT1.Vcc
  N2: Componente1.GND, RHT1.GND_2
